# Fritzing sketch midi-x-connect (saved by Fritzing 0.9.10b)
circuit board: 9.6351cm x 2.02643cm
breadboards: 1

parts:
  Arduino_Micro_1 = Arduino Micro (Rev3)
  Arduino_Micro_2 = Arduino Micro (Rev3)

nets:
  N1: Arduino_Micro_1.D1/TX, Arduino_Micro_2.D0/RX
  N2: Arduino_Micro_1.D0/RX, Arduino_Micro_2.D1/TX
  GND: Arduino_Micro_1.GND, Arduino_Micro_2.GND
